# Fritzing sketch electronic_design (saved by Fritzing 0.9.9b)
breadboards: 1

parts:
  J1 = Basic Servo
  J2 = Basic Servo
  M3 = gear-motor
  Part2 = Motor Driver 1A Dual TB6612FNG
  M4 = gear-motor
  U1 = LIPO-2000mAh [package=lipo-2000]
  Part6 = Breakout Board for Electret Microphone  # not connected
  BAT1 = BC9VPC [package=bc9vpc]  # not connected
  M5 = fc-51 [package=THT]
  M6 = fc-51 [package=THT]
  U2 = TCM8240MD [package=tcm8240md]  # not connected
  Jetson_Nano1 = jetsonnano
  Part7 = Arduino Mega 2560 (Rev3)
  U3 = Graphical LCD 128x64 [package=lcd-g12864]  # not connected
  PWM1 = PCA9685 16x12-bit PWM Breakout
  M7 = fc-51 [package=THT]

nets:
  N1: J1.pulse, PWM1.no_name_yet#7
  N2: J2.pulse, PWM1.no_name_yet#0
  N3: M3.pin_1, Part2.A02
  N4: M3.pin_2, Part2.A01
  N5: Part2.GND, U1.-, PWM1.no_name_yet#100, PWM1.no_name_yet#107, PWM1.no_name_yet#706
  N6: Part2.B01, M4.pin_1
  N7: Part2.B02, M4.pin_2
  N8: Part2.VCC, M5.pin3, M6.pin3, Jetson_Nano1.connector38, PWM1.no_name_yet#605, M7.pin3
  N9: Part2.VM, U1.+, M5.pin2, M6.pin2, Jetson_Nano1.connector37, PWM1.no_name_yet#601, PWM1.no_name_yet#602, PWM1.no_name_yet#701, PWM1.no_name_yet#1000, PWM1.no_name_yet#1007, M7.pin2
  N10: Part2.PWMA, Jetson_Nano1.connector15
  N11: Part2.AIN2, Jetson_Nano1.connector21
  N12: Part2.AIN1, Jetson_Nano1.connector17
  N13: Part2.STBY, Jetson_Nano1.connector20
  N14: Part2.BIN1, Jetson_Nano1.connector16
  N15: Part2.BIN2, Jetson_Nano1.connector24
  N16: Part2.PWMB, Jetson_Nano1.connector18
  N17: M5.pin1, Jetson_Nano1.connector6
  N18: M6.pin1, Jetson_Nano1.connector32
  N19: Jetson_Nano1.connector2, Part7.A8
  N20: Jetson_Nano1.connector9, PWM1.no_name_yet#604
  N21: Jetson_Nano1.connector29, PWM1.no_name_yet#603
  N22: Jetson_Nano1.connector34, M7.pin1
  N23: Jetson_Nano1.connector35, Part7.A10
  N24: Jetson_Nano1.connector36, Part7.A9
